# Fritzing sketch Combined_PCB_design (saved by Fritzing 0.9.3b)
circuit board: 15cm x 15cm
breadboards: 1

parts:
  U1 = 74HC4052 [package=dil16]
  J1 = JST-B3P-VH [part_number=JST-B3P-VH package=THT]
  J2 = JST-B3P-VH [part_number=JST-B3P-VH package=THT]
  J3 = JST-B3P-VH [part_number=JST-B3P-VH package=THT]
  J4 = JST-B3P-VH [part_number=JST-B3P-VH package=THT]
  J5 = JST-B3P-VH [part_number=JST-B3P-VH package=THT]
  J6 = JST-B3P-VH [part_number=JST-B3P-VH package=THT]
  J7 = JST-B3P-VH [part_number=JST-B3P-VH package=THT]
  J8 = JST-B3P-VH [part_number=JST-B3P-VH package=THT]
  J9 = Screw terminal - 2 pins [package=THT]
  J10 = Camdenboss CTB0158-4 [part_number=CTB0158-4 package=THT]
  R3 = Resistor [tolerance=±5% resistance=220 package=THT]
  R4 = Photocell (LDR) [package=THT]
  V2 = DC Power [voltage=5]
  J11 = JST-B3P-VH [part_number=JST-B3P-VH package=THT]
  R5 = Resistor [tolerance=±5% resistance=220 package=THT]
  R6 = Photocell (LDR) [package=THT]
  J12 = JST-B3P-VH [part_number=JST-B3P-VH package=THT]
  R7 = Resistor [tolerance=±5% resistance=220 package=THT]
  R8 = Photocell (LDR) [package=THT]
  J13 = JST-B3P-VH [part_number=JST-B3P-VH package=THT]
  R9 = Resistor [tolerance=±5% resistance=220 package=THT]
  R10 = Photocell (LDR) [package=THT]
  J14 = JST-B3P-VH [part_number=JST-B3P-VH package=THT]
  R11 = Resistor [tolerance=±5% resistance=220 package=THT]
  R12 = Photocell (LDR) [package=THT]
  J15 = JST-B3P-VH [part_number=JST-B3P-VH package=THT]
  R13 = Resistor [tolerance=±5% resistance=220 package=THT]
  R14 = Photocell (LDR) [package=THT]
  J16 = JST-B3P-VH [part_number=JST-B3P-VH package=THT]
  R15 = Resistor [tolerance=±5% resistance=220 package=THT]
  R16 = Photocell (LDR) [package=THT]
  J17 = JST-B3P-VH [part_number=JST-B3P-VH package=THT]
  R17 = Resistor [tolerance=±5% resistance=220 package=THT]
  R18 = Photocell (LDR) [package=THT]
  J18 = JST-B3P-VH [part_number=JST-B3P-VH package=THT]

nets:
  N1: U1.Y0, J8.pin2
  N2: U1.Y2, J7.pin2
  N3: U1.Y, J10.pin4
  N4: U1.Y3, J6.pin2
  N5: U1.Y1, J5.pin2
  N6: U1.INH, U1.VEE, U1.GND, J1.pin3, J2.pin3, J3.pin3, J4.pin3, J5.pin3, J6.pin3, J7.pin3, J8.pin3, J9.pin2
  N7: U1.B, J10.pin2
  N8: U1.A, J10.pin3
  N9: U1.X3, J4.pin2
  N10: U1.X0, J3.pin2
  N11: U1.X, J10.pin1
  N12: U1.X1, J2.pin2
  N13: U1.X2, J1.pin2
  N14: U1.VCC, J1.pin1, J2.pin1, J3.pin1, J4.pin1, J5.pin1, J6.pin1, J7.pin1, J8.pin1, J9.pin1
  N15: R3.Pin_0, V2.V-, J11.pin3
  N16: R3.Pin_1, R4.pin_0, J11.pin2
  N17: R4.pin_1, V2.V+, J11.pin1
  N18: R5.Pin_0, J12.pin3
  N19: R5.Pin_1, R6.pin_0, J12.pin2
  N20: R6.pin_1, J12.pin1
  N21: R7.Pin_0, J13.pin3
  N22: R7.Pin_1, R8.pin_0, J13.pin2
  N23: R8.pin_1, J13.pin1
  N24: R9.Pin_0, J14.pin3
  N25: R9.Pin_1, R10.pin_0, J14.pin2
  N26: R10.pin_1, J14.pin1
  N27: R11.Pin_0, J15.pin3
  N28: R11.Pin_1, R12.pin_0, J15.pin2
  N29: R12.pin_1, J15.pin1
  N30: R13.Pin_0, J16.pin3
  N31: R13.Pin_1, R14.pin_0, J16.pin2
  N32: R14.pin_1, J16.pin1
  N33: R15.Pin_0, J17.pin3
  N34: R15.Pin_1, R16.pin_0, J17.pin2
  N35: R16.pin_1, J17.pin1
  N36: R17.Pin_0, J18.pin3
  N37: R17.Pin_1, R18.pin_0, J18.pin2
  N38: R18.pin_1, J18.pin1
