# Fritzing sketch laser_harp (saved by Fritzing 0.9.3b)
circuit board: 2.4cm x 3.2cm
breadboards: 1

parts:
  R1 = Resistor [tolerance=±5% resistance=220 package=THT]
  R2 = Photocell (LDR) [package=THT]
  V1 = DC Power [voltage=5]
  J2 = JST-B3P-VH [part_number=JST-B3P-VH package=THT]

nets:
  N1: R1.Pin_0, V1.V-, J2.pin3
  N2: R1.Pin_1, R2.pin_0, J2.pin2
  N3: R2.pin_1, V1.V+, J2.pin1
