# Fritzing sketch MCB_pcb (saved by Fritzing 0.9.3b)
circuit board: 8cm x 6.5cm
breadboards: 1

parts:
  U1 = 74HC4052 [package=dil16]
  J1 = JST-B3P-VH [part_number=JST-B3P-VH package=THT]
  J2 = JST-B3P-VH [part_number=JST-B3P-VH package=THT]
  J3 = JST-B3P-VH [part_number=JST-B3P-VH package=THT]
  J4 = JST-B3P-VH [part_number=JST-B3P-VH package=THT]
  J5 = JST-B3P-VH [part_number=JST-B3P-VH package=THT]
  J6 = JST-B3P-VH [part_number=JST-B3P-VH package=THT]
  J7 = JST-B3P-VH [part_number=JST-B3P-VH package=THT]
  J8 = JST-B3P-VH [part_number=JST-B3P-VH package=THT]
  J9 = Screw terminal - 2 pins [package=THT]
  J10 = Camdenboss CTB0158-4 [part_number=CTB0158-4 package=THT]

nets:
  N1: U1.Y0, J8.pin2
  N2: U1.Y2, J7.pin2
  N3: U1.Y, J10.pin4
  N4: U1.Y3, J6.pin2
  N5: U1.Y1, J5.pin2
  N6: U1.INH, U1.VEE, U1.GND, J1.pin3, J2.pin3, J3.pin3, J4.pin3, J5.pin3, J6.pin3, J7.pin3, J8.pin3, J9.pin2
  N7: U1.B, J10.pin2
  N8: U1.A, J10.pin3
  N9: U1.X3, J4.pin2
  N10: U1.X0, J3.pin2
  N11: U1.X, J10.pin1
  N12: U1.X1, J2.pin2
  N13: U1.X2, J1.pin2
  N14: U1.VCC, J1.pin1, J2.pin1, J3.pin1, J4.pin1, J5.pin1, J6.pin1, J7.pin1, J8.pin1, J9.pin1
